# Fritzing sketch esquema (saved by Fritzing 0.9.3b)

parts:
  U1 = ESP8266 WiFi Module [part_number=ESP8266]
  IC1 = Voltage Regulator AMS1117 [package=sot223]
  R1 = Resistor [tolerance=±5% resistance=10k package=THT]

nets:
  N1: U1.VCC, IC1.IN, R1.Pin_1
  N2: U1.CH_PD, R1.Pin_0
  N3: U1.GND, IC1.OUT

notes:
  12V MAX
  3.3V
  IR signal

custom parts:
  ESP8266 WiFi Module: Generic WiFi Module based on the ESP8266 with onboard PCB antenna and UART communications
